// Logisim project NSU-2023-T04L1e09.circ as structural Verilog: 1 circuit, main circuit mycircuit
module mycircuit (
  input  A,
  input  B,
  input  C,
  output R
);

  wire not_1_out;

  assign R = not_1_out ? A : 1'bz;  // Controlled_Buffer controlled_buffer_1
  not not_1 (not_1_out, C);
endmodule
