// Logisim project NSU-2023-T04L1e11.circ as structural Verilog: 1 circuit, main circuit mycircuit
module mycircuit (
  input  A,
  input  B,
  input  C,
  output R
);

  wire nand_1_out, or_1_out;

  or or_1 (or_1_out, B, A);
  nand nand_1 (nand_1_out, A, B);
  and and_1 (R, or_1_out, nand_1_out);
endmodule
